# Fritzing sketch SIM800L-Serial (saved by Fritzing 0.9.10b)
circuit board: 8.46667cm x 5.64444cm
breadboards: 1

parts:
  M1 = sim800L v2 evb
  USBTTL1 = USB TTL Serial Cable
  M2 = sim800L v2 evb
  Mod1 = Amica NodeMCU DEVKIT 1.0
  DHT1 = DHT11 Humitidy and Temperature Sensor

nets:
  N1: M1.pin_2, M1.pin_6, USBTTL1.GND
  N2: M1.pin_3, USBTTL1.RX
  N3: M1.pin_4, USBTTL1.TX
  N4: M1.pin_7, USBTTL1.5V
  N5: M2.pin_2, M2.pin_6, Mod1.pin2, Mod1.pin_9, Mod1.pin_25, Mod1.pin_29, DHT1.GND
  N6: M2.pin_3, Mod1.pin8
  N7: M2.pin_4, Mod1.pin7
  N8: M2.pin_5, Mod1.pin1, Mod1.pin_10, Mod1.pin_26, DHT1.VDD
  N9: Mod1.pin_12, DHT1.DATA

custom parts:
  sim800L v2 evb: sim800L v2 evb GSM module.
  DHT11 Humitidy and Temperature Sensor: DHT11 Humidity and Temperature Sensor
